// Logisim project lab6.circ as structural Verilog: 2 circuits, main circuit main
module main (
  input  roll2107071,
  input  in_2,
  input  in_3,
  input  in_4,
  input  in_5,
  output out_6,
  output out_7,
  output out_8,
  output out_9
);

  Bin2Excess3 bin2excess3_1 (
    .B0(in_2), .B1(in_3), .B2(in_4), .B3(in_5), .E0(out_6), .E1(out_7), .E2(out_8), .E3(out_9));
endmodule

module Bin2Excess3 (
  input  B0,
  input  B1,
  input  B2,
  input  B3,
  output E0,
  output E1,
  output E2,
  output E3
);

  wire and_1_out, or_1_out;

  or or_1 (or_1_out, B0, B1);
  and and_1 (and_1_out, or_1_out, B2);
  not not_1 (E0, B0);
  xnor xnor_1 (E1, B0, B1);
  xor xor_1 (E2, or_1_out, B2);
  or or_2 (E3, and_1_out, B3);
endmodule
