// Logisim project lab_assign.circ as structural Verilog: 4 circuits, main circuit main
module main (
  input  [3:0] in_1,
  input  [3:0] in_2
);

  wire blk4_1_eq, blk4_1_gt, blk4_1_lt;

  // Probe on in_1
  // Probe on in_2
  blk4 blk4_1 (
    .a3(in_1[3]), .a2(in_1[2]), .a1(in_1[1]), .a0(in_1[0]), .b3(in_2[3]), .b2(in_2[2]), .b1(in_2[1]),
    .b0(in_2[0]), .lt(blk4_1_lt), .eq(blk4_1_eq), .gt(blk4_1_gt));
  // RGBLED rgbled_1: pin names not known; wires that end beside it: blk4_1_eq, blk4_1_lt, blk4_1_gt

  // Notes on the sheet:
  //   2107071
  //   red = equal
  //   green = less than
  //   blue = greater than
endmodule

module blk (
  input  a,
  input  b,
  output lt,
  output eq,
  output gt
);

  wire or_1_out;

  and and_1 (lt, ~a, b);  // AND_Gate
  and and_2 (gt, a, ~b);  // AND_Gate
  or or_1 (or_1_out, lt, gt);
  not not_1 (eq, or_1_out);

  // Notes on the sheet:
  //   2107071
endmodule

module blk2 (
  input  a1,
  input  b1,
  input  a0,
  input  b0,
  output lt,
  output eq,
  output gt
);

  wire and_1_out, and_3_out, g0, g1, l0, l1, x0, x1;

  blk blk_1 (.a(a1), .b(b1), .lt(l1), .eq(x1), .gt(g1));
  blk blk_2 (.a(a0), .b(b0), .lt(l0), .eq(x0), .gt(g0));
  and and_1 (and_1_out, x1, l0);
  and and_2 (eq, x1, x0);
  and and_3 (and_3_out, x1, g0);
  or or_1 (lt, and_1_out, l1);
  or or_2 (gt, and_3_out, g1);

  // Notes on the sheet:
  //   2107071
endmodule

module blk4 (
  input  a3,
  input  a2,
  input  a1,
  input  a0,
  input  b3,
  input  b2,
  input  b1,
  input  b0,
  output lt,
  output eq,
  output gt
);

  wire and_2_out, and_3_out, g0, g1, l0, l1, x0, x1;

  blk2 blk2_1 (.a1(a3), .b1(b3), .a0(a2), .b0(b2), .lt(l1), .eq(x1), .gt(g1));
  blk2 blk2_2 (.a1(a1), .b1(b1), .a0(a0), .b0(b0), .lt(l0), .eq(x0), .gt(g0));
  and and_1 (eq, x1, x0);
  and and_2 (and_2_out, x1, l0);
  or or_1 (lt, and_2_out, l1);
  and and_3 (and_3_out, x1, g0);
  or or_2 (gt, and_3_out, g1);

  // Notes on the sheet:
  //   2107071
endmodule
