// Logisim project assign.circ as structural Verilog: 3 circuits, main circuit main
module main (
  input  in_1,
  input  in_2
);

  wire clk, d0, d0p, d1, d1p, d2, d2p, di1, di2, or_1_out;

  Clock clock_1 (.out(clk));
  // Probe on {d2, d1, d0}
  Dp dp_1 (.preset(in_1), .di(d0p), .clk(clk), .reset(in_2), .\do (d0), .dop(d0p));
  Dp dp_2 (.preset(in_1), .di(di1), .clk(clk), .reset(in_2), .\do (d1), .dop(d1p));
  Dp dp_3 (.preset(in_1), .di(di2), .clk(clk), .reset(in_2), .\do (d2), .dop(d2p));
  xnor xnor_1 (di1, d1, d0);
  xnor xnor_2 (di2, d2, or_1_out);
  or or_1 (or_1_out, d1, d0);

  // Other names for the same wires on the sheet: di0 = d0p; preset = in_1; reset = in_2

  // Notes on the sheet:
  //   2107071
endmodule

module D (
  input  preset,
  input  di,
  input  clk,
  input  reset,
  output \do ,
  output dop
);

  wire nand_1_out, nand_2_out, not_1_out;

  not not_1 (not_1_out, di);
  nand nand_1 (nand_1_out, di, clk);
  nand nand_2 (nand_2_out, clk, not_1_out);
  nand nand_3 (\do , preset, nand_1_out, dop);
  nand nand_4 (dop, \do , nand_2_out, reset);

  // Notes on the sheet:
  //   2107071
endmodule

module Dp (
  input  preset,
  input  di,
  input  clk,
  input  reset,
  output \do ,
  output dop
);

  wire d_1_do, not_1_out;

  not not_1 (not_1_out, clk);
  D d_1 (.preset(preset), .di(di), .clk(clk), .reset(reset), .\do (d_1_do));  // open: dop
  D d_2 (.preset(preset), .di(d_1_do), .clk(not_1_out), .reset(reset), .\do (\do ), .dop(dop));

  // Notes on the sheet:
  //   2107071
endmodule
