// Logisim project hex27.circ as structural Verilog: 9 circuits, main circuit main
module main (
  input  [3:0] in_1
);

  wire deco_1_oa, deco_1_ob, deco_1_oc, deco_1_od, deco_1_oe, deco_1_ofo, deco_1_og;

  deco deco_1 (
    .in_1(in_1), .oa(deco_1_oa), .ob(deco_1_ob), .oc(deco_1_oc), .od(deco_1_od), .oe(deco_1_oe),
    .ofo(deco_1_ofo), .og(deco_1_og));
  _7_Segment_Display u_7_segment_display_1 (
    .g(deco_1_og), .f(deco_1_ofo), .a(deco_1_oa), .b(deco_1_ob), .e(deco_1_oe), .d(deco_1_od), .c(deco_1_oc));  // open: dp
endmodule

module a (
  input  [3:0] in_1,
  output a7
);

  wire and_1_out, and_2_out, and_3_out, and_4_out, and_5_out, and_6_out;

  and and_1 (and_1_out, in_1[3], ~in_1[2], ~in_1[1]);  // AND_Gate
  and and_2 (and_2_out, in_1[2], in_1[1]);
  and and_3 (and_3_out, ~in_1[2], ~in_1[0]);  // AND_Gate
  and and_4 (and_4_out, ~in_1[3], in_1[1]);  // AND_Gate
  and and_5 (and_5_out, in_1[3], ~in_1[0]);  // AND_Gate
  and and_6 (and_6_out, ~in_1[3], in_1[2], in_1[0]);  // AND_Gate
  or or_1 (a7, and_1_out, and_2_out, and_3_out, and_4_out, and_5_out, and_6_out);
endmodule

module b (
  input  [3:0] in_1,
  output out_2
);

  wire and_1_out, and_2_out, and_3_out, and_4_out, and_5_out;

  and and_1 (and_1_out, ~in_1[2], ~in_1[1]);  // AND_Gate
  and and_2 (and_2_out, ~in_1[0], ~in_1[2]);  // AND_Gate
  and and_3 (and_3_out, ~in_1[3], ~in_1[1], ~in_1[0]);  // AND_Gate
  and and_4 (and_4_out, in_1[3], ~in_1[1], in_1[0]);  // AND_Gate
  and and_5 (and_5_out, ~in_1[3], in_1[1], in_1[0]);  // AND_Gate
  or or_1 (out_2, and_1_out, and_2_out, and_3_out, and_4_out, and_5_out);

  // Notes on the sheet:
  //   2107071
endmodule

module c (
  input  [3:0] in_1,
  output out_2
);

  wire and_1_out, and_2_out, and_3_out, and_4_out, and_5_out;

  and and_1 (and_1_out, in_1[3], ~in_1[2]);  // AND_Gate
  and and_2 (and_2_out, ~in_1[1], in_1[0]);  // AND_Gate
  and and_3 (and_3_out, ~in_1[2], ~in_1[1]);  // AND_Gate
  and and_4 (and_4_out, in_1[0], ~in_1[3]);  // AND_Gate
  and and_5 (and_5_out, ~in_1[3], in_1[2]);  // AND_Gate
  or or_1 (out_2, and_1_out, and_2_out, and_3_out, and_4_out, and_5_out);

  // Notes on the sheet:
  //   2107071
endmodule

module d (
  input  [3:0] in_1,
  output out_2
);

  wire and_1_out, and_2_out, and_3_out, and_4_out, and_5_out;

  and and_1 (and_1_out, ~in_1[3], ~in_1[2], ~in_1[0]);  // AND_Gate
  and and_2 (and_2_out, ~in_1[2], in_1[1], in_1[0]);  // AND_Gate
  and and_3 (and_3_out, ~in_1[1], in_1[2], in_1[0]);  // AND_Gate
  and and_4 (and_4_out, in_1[3], ~in_1[1]);  // AND_Gate
  and and_5 (and_5_out, ~in_1[0], in_1[2], in_1[1]);  // AND_Gate
  or or_1 (out_2, and_1_out, and_2_out, and_3_out, and_4_out, and_5_out);

  // Notes on the sheet:
  //   2107071
endmodule

module e (
  input  [3:0] in_1,
  output out_2
);

  wire and_1_out, and_2_out, and_3_out, and_4_out;

  and and_1 (and_1_out, ~in_1[2], ~in_1[0]);  // AND_Gate
  and and_2 (and_2_out, in_1[3], in_1[2]);
  and and_3 (and_3_out, ~in_1[0], in_1[1]);  // AND_Gate
  and and_4 (and_4_out, in_1[3], in_1[1]);
  or or_1 (out_2, and_1_out, and_2_out, and_3_out, and_4_out);

  // Notes on the sheet:
  //   2107071
endmodule

module f (
  input  [3:0] in_1,
  output out_2
);

  wire and_1_out, and_2_out, and_3_out, and_4_out, and_5_out;

  and and_1 (and_1_out, ~in_1[1], ~in_1[0]);  // AND_Gate
  and and_2 (and_2_out, in_1[3], ~in_1[2]);  // AND_Gate
  and and_3 (and_3_out, ~in_1[0], in_1[2]);  // AND_Gate
  and and_4 (and_4_out, in_1[3], in_1[2], in_1[1]);
  and and_5 (and_5_out, ~in_1[3], ~in_1[1], in_1[2]);  // AND_Gate
  or or_1 (out_2, and_1_out, and_2_out, and_3_out, and_4_out, and_5_out);

  // Notes on the sheet:
  //   2107071
endmodule

module g (
  input  [3:0] in_1,
  output out_2
);

  wire and_1_out, and_2_out, and_3_out, and_4_out, and_5_out;

  and and_1 (and_1_out, in_1[3], ~in_1[2]);  // AND_Gate
  and and_2 (and_2_out, in_1[1], ~in_1[0]);  // AND_Gate
  and and_3 (and_3_out, in_1[3], in_1[0]);
  and and_4 (and_4_out, ~in_1[3], in_1[2], ~in_1[1]);  // AND_Gate
  and and_5 (and_5_out, ~in_1[2], in_1[1]);  // AND_Gate
  or or_1 (out_2, and_1_out, and_2_out, and_3_out, and_4_out, and_5_out);

  // Notes on the sheet:
  //   2107071
endmodule

module deco (
  input  [3:0] in_1,
  output oa,
  output ob,
  output oc,
  output od,
  output oe,
  output ofo,
  output og
);

  a a_1 (.in_1(in_1), .a7(oa));
  b b_1 (.in_1(in_1), .out_2(ob));
  c c_1 (.in_1(in_1), .out_2(oc));
  e e_1 (.in_1(in_1), .out_2(oe));
  f f_1 (.in_1(in_1), .out_2(ofo));
  g g_1 (.in_1(in_1), .out_2(og));
  d d_1 (.in_1(in_1), .out_2(od));
endmodule
