// Logisim project project_safe.circ as structural Verilog: 11 circuits, main circuit flip4
module main (
);

  wire and_1_out, and_2_out, and_3_out, and_4_out, CC, change, changeHOUR, changeMeridian, changeMIN,
       changeSEC, clk, H, hour_1_complete, hour_1_h1, hour_1_h1p, M, m_t, MC, Mr, or_1_out, or_2_out,
       or_3_out, pause, S, y_1_a, y_1_b, y_1_c, y_1_d, y_1_e, y_1_f, y_1_g, y_2_a, y_2_b, y_2_c, y_2_d,
       y_2_e, y_2_f, y_2_g, y_3_a, y_3_b, y_3_c, y_3_d, y_3_e, y_3_f, y_3_g, y_4_a, y_4_b, y_4_c, y_4_d,
       y_4_e, y_4_f, y_4_g, y_5_a, y_5_b, y_5_c, y_5_d, y_5_e, y_5_f, y_5_g, y_6_a, y_6_b, y_6_c, y_6_d,
       y_6_e, y_6_f, y_6_g;
  wire [2:0] blk_1_o1, blk_1_o1p, blk_2_o1, blk_2_o1p;
  wire [3:0] blk_1_o0, blk_1_o0p, blk_2_o0, blk_2_o0p, hour_1_q, hour_1_qp;
  wire [6:0] h0, h1, m0, m1, s0, s1;

  DipSwitch #(.number(2)) dipswitch_1 (.sw1(pause), .sw2(change));
  Clock clock_1 (.out(clk));
  _7_Segment_Display u_7_segment_display_1 (
    .g(y_1_g), .f(y_1_f), .a(y_1_a), .b(y_1_b), .e(y_1_e), .d(y_1_d), .c(y_1_c));  // open: dp
  y y_1 (.in_1(h1), .a(y_1_a), .c(y_1_c), .e(y_1_e), .g(y_1_g), .b(y_1_b), .d(y_1_d), .f(y_1_f));
  or or_1 (or_1_out, changeSEC, and_1_out);
  and and_1 (and_1_out, clk, ~pause);  // AND_Gate
  or or_2 (or_2_out, changeMIN, and_2_out);
  and and_2 (and_2_out, CC, ~pause);  // AND_Gate
  or or_3 (or_3_out, changeHOUR, and_3_out);
  and and_3 (and_3_out, MC, ~pause);  // AND_Gate
  Button button_1 (.out(H));
  _7_Segment_Display u_7_segment_display_2 (
    .g(y_2_g), .f(y_2_f), .a(y_2_a), .b(y_2_b), .e(y_2_e), .d(y_2_d), .c(y_2_c));  // open: dp
  y y_2 (.in_1(h0), .a(y_2_a), .c(y_2_c), .e(y_2_e), .g(y_2_g), .b(y_2_b), .d(y_2_d), .f(y_2_f));
  blink blink_1 (.in_1(clk));
  _7_Segment_Display u_7_segment_display_3 (
    .g(y_3_g), .f(y_3_f), .a(y_3_a), .b(y_3_b), .e(y_3_e), .d(y_3_d), .c(y_3_c));  // open: dp
  _7_Segment_Display u_7_segment_display_4 (
    .g(y_4_g), .f(y_4_f), .a(y_4_a), .b(y_4_b), .e(y_4_e), .d(y_4_d), .c(y_4_c));  // open: dp
  y y_3 (.in_1(m1), .a(y_3_a), .c(y_3_c), .e(y_3_e), .g(y_3_g), .b(y_3_b), .d(y_3_d), .f(y_3_f));
  y y_4 (.in_1(m0), .a(y_4_a), .c(y_4_c), .e(y_4_e), .g(y_4_g), .b(y_4_b), .d(y_4_d), .f(y_4_f));
  Button button_2 (.out(M));
  _7_Segment_Display u_7_segment_display_5 (
    .g(y_5_g), .f(y_5_f), .a(y_5_a), .b(y_5_b), .e(y_5_e), .d(y_5_d), .c(y_5_c));  // open: dp
  y y_5 (.in_1(s1), .a(y_5_a), .c(y_5_c), .e(y_5_e), .g(y_5_g), .b(y_5_b), .d(y_5_d), .f(y_5_f));
  blink blink_2 (.in_1(clk));
  blk blk_1 (.clk(or_1_out), .complete(CC), .o0(blk_1_o0), .o0p(blk_1_o0p), .o1(blk_1_o1), .o1p(blk_1_o1p));
  blk blk_2 (.clk(or_2_out), .complete(MC), .o0(blk_2_o0), .o0p(blk_2_o0p), .o1(blk_2_o1), .o1p(blk_2_o1p));
  hour hour_1 (
    .clk(or_3_out), .q(hour_1_q), .qp(hour_1_qp), .h1(hour_1_h1), .h1p(hour_1_h1p), .complete(hour_1_complete));
  Button button_3 (.out(S));
  _7_Segment_Display u_7_segment_display_6 (
    .g(y_6_g), .f(y_6_f), .a(y_6_a), .b(y_6_b), .e(y_6_e), .d(y_6_d), .c(y_6_c));  // open: dp
  y y_6 (.in_1(s0), .a(y_6_a), .c(y_6_c), .e(y_6_e), .g(y_6_g), .b(y_6_b), .d(y_6_d), .f(y_6_f));
  seg7 seg7_1 (.q(blk_1_o0), .in_2(blk_1_o0p), .s(s0));
  seg73 seg73_1 (.s(blk_1_o1), .in_2(blk_1_o1p), .t(s1));
  seg7 seg7_2 (.q(blk_2_o0), .in_2(blk_2_o0p), .s(m0));
  seg73 seg73_2 (.s(blk_2_o1), .in_2(blk_2_o1p), .t(m1));
  seg7 seg7_3 (.q(hour_1_q), .in_2(hour_1_qp), .s(h0));
  seg12 seg12_1 (.a(hour_1_h1), .ap(hour_1_h1p), .t(h1));
  and and_4 (and_4_out, hour_1_complete, ~pause);  // AND_Gate
  Button button_4 (.out(Mr));
  meridian meridian_1 (.m(m_t));
  or or_4 (m_t, and_4_out, changeMeridian);
  and and_5 (changeHOUR, change, H);
  and and_6 (changeMIN, change, M);
  and and_7 (changeSEC, change, S);
  and and_8 (changeMeridian, change, Mr);

  // Notes on the sheet:
  //   2107071
endmodule

module flip4 (
  input  clk,
  input  isother1,
  output [3:0] q,
  output [3:0] qp,
  output complete
);

  wire and_1_out, and_2_out, isthis1, skip, t0, t1, t2, t3;

  T_Flip_Flop t_ff_1 (.T(t0), .clk(clk), .Q(q[3]), .Qn(qp[3]));  // open: reset, preset
  and and_1 (and_1_out, q[2], q[1], q[0]);
  and and_2 (and_2_out, q[3], q[0]);
  and and_3 (t1, q[1], q[0]);
  and and_4 (t2, qp[3], q[0]);
  and and_5 (skip, isthis1, isother1);
  T_Flip_Flop t_ff_2 (.T(t1), .clk(clk), .Q(q[2]), .Qn(qp[2]));  // open: reset, preset
  or or_1 (t0, and_1_out, and_2_out);
  T_Flip_Flop t_ff_3 (.T(t2), .clk(clk), .Q(q[1]), .Qn(qp[1]));  // open: reset, preset
  T_Flip_Flop t_ff_4 (.T(t3), .clk(clk), .Q(q[0]), .Qn(qp[0]));  // open: reset, preset
  not not_1 (t3, skip);
  and and_6 (complete, q[3], qp[2], qp[1], q[0]);
  and and_7 (isthis1, qp[3], qp[2], qp[1], q[0]);

  // Other names for the same wires on the sheet: q3 = q[0]; q2 = q[1]; q1 = q[2]; q0 = q[3]; qp3 = qp[0]; qp2 = qp[1];
  //   qp1 = qp[2]; qp0 = qp[3]; z0 = t0; z1 = t1; z2 = t2

  // Notes on the sheet:
  //   2107071
  //   notation in reverse
endmodule

module flip3 (
  input  clk,
  output [2:0] q,
  output [2:0] qp,
  output is5,
  output is1
);

  wire a1, and_3_out, and_4_out, and_5_out, t0, t1, t2;

  T_Flip_Flop #(.trigger("falling")) t_ff_1 (.T(t0), .clk(clk), .Q(q[0]), .Qn(qp[0]));  // open: reset, preset
  and and_1 (is5, q[0], qp[1], q[2]);
  T_Flip_Flop #(.trigger("falling")) t_ff_2 (.T(t1), .clk(clk), .Q(q[1]), .Qn(qp[1]));  // open: reset, preset
  T_Flip_Flop #(.trigger("falling")) t_ff_3 (.T(t2), .clk(clk), .Q(q[2]), .Qn(qp[2]));  // open: reset, preset
  and and_2 (a1, q[1], q[0]);
  and and_3 (and_3_out, q[2], q[0]);
  and and_4 (and_4_out, q[2], q[1]);
  and and_5 (and_5_out, qp[2], q[0]);
  or or_1 (t0, qp[2], qp[1]);
  and and_6 (is1, q[0], qp[1], qp[2]);
  or or_2 (t2, a1, and_3_out, and_4_out);
  or or_3 (t1, and_5_out, a1);

  // Notes on the sheet:
  //   2107071
endmodule

module hour (
  input  clk,
  output [3:0] q,
  output [3:0] qp,
  output h1,
  output h1p,
  output complete
);

  wire and_1_out, and_2_out, comp10, is2, t0, t1, t2;

  and and_1 (and_1_out, q[2], q[1], q[0]);
  and and_2 (and_2_out, q[3], q[0]);
  and and_3 (t1, q[1], q[0]);
  and and_4 (t2, qp[3], q[0]);
  T_Flip_Flop #(.trigger("falling")) t_ff_1 (
    .T(t0), .clk(clk), .Q(q[3]), .Qn(qp[3]), .reset(complete));  // open: preset
  or or_1 (t0, and_1_out, and_2_out);
  T_Flip_Flop #(.trigger("falling")) t_ff_2 (
    .T(t1), .clk(clk), .Q(q[2]), .Qn(qp[2]), .reset(complete));  // open: preset
  T_Flip_Flop #(.trigger("falling")) t_ff_3 (
    .T(t2), .clk(clk), .Q(q[1]), .Qn(qp[1]), .reset(complete));  // open: preset
  and and_5 (comp10, q[3], qp[0], q[1], qp[2]);
  and and_6 (is2, qp[3], qp[2], q[1], qp[0]);
  and and_7 (complete, h1, is2);
  T_Flip_Flop t_ff_4 (.T(comp10), .clk(clk), .Q(h1), .Qn(h1p), .reset(complete));  // open: preset
  T_Flip_Flop #(.trigger("falling")) t_ff_5 (
    .T(1'b1), .clk(clk), .Q(q[0]), .Qn(qp[0]), .reset(complete));  // open: preset

  // Other names for the same wires on the sheet: q3 = q[0]; q2 = q[1]; q1 = q[2]; q0 = q[3]; qp3 = qp[0]; qp2 = qp[1];
  //   qp1 = qp[2]; qp0 = qp[3]; reset = complete

  // Notes on the sheet:
  //   2107071
  //   reverse
endmodule

module blk (
  input  clk,
  output complete,
  output [3:0] o0,
  output [3:0] o0p,
  output [2:0] o1,
  output [2:0] o1p
);

  wire M1, M5, SC;

  and and_1 (complete, M5, SC);
  flip4 flip4_1 (.clk(clk), .isother1(M1), .q(o0), .qp(o0p), .complete(SC));
  flip3 flip3_1 (.clk(SC), .q(o1), .qp(o1p), .is5(M5), .is1(M1));

  // Notes on the sheet:
  //   2107071
endmodule

module seg7 (
  input  [3:0] q,
  input  [3:0] in_2,
  output [6:0] s
);

  wire and_10_out, and_11_out, Q0Q1, Q1q0, q1q0_t, Q2Q0, Q2q0_t, q2q0_t_t, Q2q1, q2Q1_t, Q3Q1;

  and and_1 (q2Q1_t, in_2[2], q[1]);
  and and_2 (Q2q1, q[2], in_2[1]);
  and and_3 (Q1q0, q[1], in_2[0]);
  and and_4 (q1q0_t, in_2[0], in_2[1]);
  and and_5 (Q2q0_t, in_2[0], q[2]);
  and and_6 (q2q0_t_t, in_2[0], in_2[2]);
  and and_7 (Q3Q1, q[3], q[1]);
  and and_8 (Q0Q1, q[1], q[0]);
  and and_9 (Q2Q0, q[2], q[0]);
  or or_1 (s[6], q2Q1_t, Q2q1, Q1q0, q[3]);
  or or_2 (s[5], q1q0_t, Q2q1, Q2q0_t, q[3]);
  and and_10 (and_10_out, Q2Q0, q[3]);
  or or_3 (s[4], and_10_out, Q3Q1, Q1q0, q2q0_t_t);
  and and_11 (and_11_out, Q2q1, q[0]);
  or or_4 (s[3], and_11_out, q[3], q2Q1_t, Q1q0, q2q0_t_t);
  or or_5 (s[2], q[0], in_2[1], q[2], q[3]);
  or or_6 (s[1], Q0Q1, q1q0_t, in_2[2]);
  or or_7 (s[0], q2q0_t_t, Q2Q0, q[1], q[3]);

  // Other names for the same wires on the sheet: p0 = in_2[0]; p1 = in_2[1]; p2 = in_2[2]; p3 = in_2[3]

  // Notes on the sheet:
  //   2107072
endmodule

module y (
  input  [6:0] in_1,
  output a,
  output b,
  output c,
  output d,
  output e,
  output f,
  output g
);


  assign a = in_1[0];
  assign b = in_1[1];
  assign c = in_1[2];
  assign d = in_1[3];
  assign e = in_1[4];
  assign f = in_1[5];
  assign g = in_1[6];

  // Notes on the sheet:
  //   2107072
endmodule

module seg73 (
  input  [2:0] s,
  input  [2:0] in_2,
  output [6:0] t
);

  wire and_1_out, and_3_out, and_4_out;

  or or_1 (t[6], s[2], s[1]);
  and and_1 (and_1_out, in_2[1], in_2[0]);
  and and_2 (t[4], in_2[2], in_2[0]);
  and and_3 (and_3_out, s[2], s[0]);
  or or_2 (t[2], in_2[1], s[0], s[2]);
  or or_3 (t[1], in_2[2], in_2[0]);
  and and_4 (and_4_out, s[2], s[0]);
  or or_4 (t[5], and_1_out, s[2]);
  or or_5 (t[3], t[4], s[1], and_3_out);
  or or_6 (t[0], s[1], and_4_out, t[4]);

  // Other names for the same wires on the sheet: j1 = t[4]

  // Notes on the sheet:
  //   2107072
endmodule

module meridian (
  input  m
);

  wire t_ff_1_q, t_ff_1_qn;

  T_Flip_Flop #(.trigger("falling")) t_ff_1 (.T(1'b1), .clk(m), .Q(t_ff_1_q), .Qn(t_ff_1_qn));  // open: reset, preset
  LED led_1 (.in(t_ff_1_q));
  LED led_2 (.in(t_ff_1_qn));
endmodule

module seg12 (
  input  a,
  input  ap,
  output [6:0] t
);


  assign t = {1'b0, {3{ap}}, 2'b11, ap};

  // Notes on the sheet:
  //   2107072
endmodule

module blink (
  input  in_1
);

  LED led_1 (.in(in_1));
  LED led_2 (.in(in_1));

  // Notes on the sheet:
  //   2107072
endmodule
